# Fritzing sketch babyTamagotchi (saved by Fritzing 0.9.3b)

parts:
  Součástka1 = Arduino Pro Mini v13
  S2 = Pushbutton [package=THT]  # not connected
  S3 = Pushbutton [package=THT]  # not connected
  R1 = Resistor [tolerance=±5% resistance=10k package=THT]  # not connected
  R2 = Resistor [tolerance=±5% resistance=10k package=THT]  # not connected
  U1 = LIPO-110mAh [package=lipo-110]
  TP1 = TP4056 [chip_label=TP4056 package="DIP (Dual Inline) [THT]"]

nets:
  N1: Součástka1.VCC, TP1.pin4
  N2: Součástka1.GND, TP1.pin5
  N3: U1.+, TP1.pin3
  N4: U1.-, TP1.pin6

custom parts:
  TP4056: A DIP stand-in part for whatever IC you want. With 6 pins on a 300mil dual inline package (DIP) footprint.
